# Fritzing sketch pico-dash (saved by Fritzing 1.0.6)
breadboards: 1

parts:
  Pico = Raspberry Pi Pico W
  TFT = ST7735 1.8 inch TFT LCD [package="SIP (Single Inline) [THT]"]
  previous_screen_button = Pushbutton [package="[THT]"]
  next_screen_button = Pushbutton [package="[THT]"]
  inc_left_button = Pushbutton [package="[THT]"]
  dec_left_button = Pushbutton [package="[THT]"]
  inc_right_button = Pushbutton [package="[THT]"]
  dec_right_button = Pushbutton [package="[THT]"]
  CONNECTED_LED = LED - 5mm [color="Red (633nm)" current=0.030A package="5 mm [THT]"]
  HERO_READY_LED = LED - 5mm [color="Green (570nm)" current=0.030A package="5 mm [THT]"]
  HERO_DONE_LED = LED - 5mm [color="Red (633nm)" current=0.030A package="5 mm [THT]"]
  HERO_ORDER_LED = LED - 5mm [color="Blue (525nm)" current=0.030A package="5 mm [THT]"]
  hero_done_button = Pushbutton [package="[THT]"]
  screen_mode_button = Pushbutton [package="[THT]"]

nets:
  N1: Pico.pin_3, Pico.pin_23, Pico.pin_28, Pico.pin_33, Pico.pin_38, TFT.GND, previous_screen_button.Pin_3, previous_screen_button.Pin_4, next_screen_button.Pin_3, next_screen_button.Pin_4, inc_left_button.Pin_3, inc_left_button.Pin_4, dec_left_button.Pin_3, dec_left_button.Pin_4, inc_right_button.Pin_3, inc_right_button.Pin_4, dec_right_button.Pin_3, dec_right_button.Pin_4, CONNECTED_LED.cathode, HERO_READY_LED.cathode, HERO_DONE_LED.cathode, HERO_ORDER_LED.cathode, hero_done_button.Pin_3, hero_done_button.Pin_4, screen_mode_button.Pin_3, screen_mode_button.Pin_4
  N2: Pico.pin_4, HERO_ORDER_LED.anode
  N3: Pico.pin_5, HERO_DONE_LED.anode
  N4: Pico.pin_6, HERO_READY_LED.anode
  N5: Pico.pin_7, CONNECTED_LED.anode
  N6: Pico.pin_11, TFT.CS
  N7: Pico.pin_14, TFT.A0
  N8: Pico.pin_15, TFT.RST
  N9: Pico.pin_16, hero_done_button.Pin_1, hero_done_button.Pin_2
  N10: Pico.pin_17, screen_mode_button.Pin_2
  N11: Pico.pin_19, TFT.SCK
  N12: Pico.pin_20, TFT.SDA
  N13: Pico.pin_21, dec_left_button.Pin_1, dec_left_button.Pin_2
  N14: Pico.pin_22, inc_left_button.Pin_1, inc_left_button.Pin_2
  N15: Pico.pin_24, dec_right_button.Pin_1, dec_right_button.Pin_2
  N16: Pico.pin_25, inc_right_button.Pin_1, inc_right_button.Pin_2
  N17: Pico.pin_26, next_screen_button.Pin_2
  N18: Pico.pin_27, previous_screen_button.Pin_2
  N19: Pico.pin_36, TFT.VCC

custom parts:
  Raspberry Pi Pico W: Raspberry Pi Pico W. Based around the RP2040 microcontroller the Pico W is a low cost microcontroller device bringing Raspberry Pi quality, cost, and easy of use to the microcontroller space. The areas marked KEEPOUT in pcb silkscreen should not have traces running through them to avoid shorts on a soldered in module!
  ST7735 1.8 inch TFT LCD: 1.8 inch TFT LCD module. SPI interface, ST7735 controller
